# Fritzing sketch microfonoSpiaWifi (saved by Fritzing 0.9.4)

parts:
  part = INMP441 [part_number=INMP441]
  part_2 = ESP32-38PinWide [part_number="ESP32-WROOM 32"]

nets:
  GND: part.L/R, part.GND, part_2.GND
  N1: part.WS, part_2.GPIO2
  N2: part.SCK, part_2.GPIO14
  N3: part.SD, part_2.GPIO15
  N4: part.VDD, part_2.3.3

notes:
  INMP441 ESP32 WROOM
  gnd gnd
  vdd vcc(3.3V)
  sd 15
  sck 14
  ws 2
  l/r gnd

custom parts:
  INMP441: This is a simple breakout board for the INMP441 I2S MEMS microphone.
  ESP32-38PinWide: Generic 38-Pin ESP32 with wide format (only access to one side of pins on a breadboard) based on Stephen Lilley's HiLetgo ESP-WROOM-32 ESP32 ESP-32S Development Board.
