# Fritzing sketch microfonoSpiaWifiConEspS2Mini (saved by Fritzing 0.9.4)

parts:
  part = INMP441 [part_number=INMP441]
  part_2 = Wemos S2 Mini [part_number="WeMos Esp32-S2 Mini"]

nets:
  N1: part.L/R, part.GND, part_2.Pin_17, part_2.Pin_18, part_2.Pin_26
  N2: part.WS, part_2.Pin_19
  N3: part.SCK, part_2.Pin_20
  N4: part.SD, part_2.Pin_5, part_2.Pin_6
  N5: part.VDD, part_2.Pin_8

notes:
  INMP441 ESP32-S2 MINI
  GND GND
  Vdd vcc(3.3V)
  SD 9
  SCK 18
  WS 16
  L/R GND

custom parts:
  INMP441: This is a simple breakout board for the INMP441 I2S MEMS microphone.
  Wemos S2 Mini: A mini wifi board based on the ESP32-S2FN4R2.
